// Logisim project control_logic.circ as structural Verilog: 1 circuit, main circuit control_logic
module control_logic (
  input  [31:0] inst,
  input  BrEq,
  input  BrLt,
  output PCSel,
  output RegWEn,
  output [2:0] ImmSel,
  output BrUn,
  output ASel,
  output BSel,
  output [3:0] ALUSel,
  output MemRW,
  output [1:0] WBSel
);


  assign ALUSel = 4'b0000;
  assign ImmSel = 3'b000;

  // Other names for the same wires on the sheet: opcode[6:0] = inst[6:0]; imm7_31[24:0] = inst[31:7];
  //   rd[4:0] = inst[11:7]; func3[2:0] = inst[14:12]; rs1[4:0] = inst[19:15]; rs2[4:0] = inst[24:20];
  //   func7[6:0] = inst[31:25]

  // Notes on the sheet:
  //   INPUTS to your circuit
  //   DON'T CHANGE THE LOCATIONS OF THE INPUTS AND OUTPUTS!
  //   OUTPUT from your circuit
endmodule
